// Logisim project adders and latches.circ as structural Verilog: 7 circuits, main circuit main
module main (
  input  in_1,
  input  in_2,
  output out_3,
  output out_4
);

  halfadder HA ();  // open: a, in_2, s, c
  dlatch D_latch (.en(in_1), .D(in_2), .out(out_4));
  fulladder FA ();  // open: a, b, s, co, ci
  clock CLOCK (.out_1(out_3));
  _8bitadder _8bit_adder ();  // open: co, in_1, in_2, in_3, in_4, in_5, in_6, in_7, in_8, in_9, in_10, in_11, in_12, in_13, in_14, in_15, in_16, out_19, out_20, out_21, out_22, out_23, out_24, out_25, out_26, in_17
endmodule

module halfadder (
  input  a,
  input  in_2,
  output s,
  output c
);

  xor xor_1 (s, a, in_2);
  and and_1 (c, a, in_2);
endmodule

module fulladder (
  input  ci,
  input  a,
  input  b,
  output s,
  output co
);

  wire halfadder_1_c, halfadder_1_s, halfadder_2_c;

  halfadder halfadder_1 (.a(a), .in_2(b), .s(halfadder_1_s), .c(halfadder_1_c));
  halfadder halfadder_2 (.a(halfadder_1_s), .in_2(ci), .s(s), .c(halfadder_2_c));
  or or_1 (co, halfadder_2_c, halfadder_1_c);
endmodule

module _8bitadder (
  input  in_1,
  input  in_2,
  input  in_3,
  input  in_4,
  input  in_5,
  input  in_6,
  input  in_7,
  input  in_8,
  input  in_9,
  input  in_10,
  input  in_11,
  input  in_12,
  input  in_13,
  input  in_14,
  input  in_15,
  input  in_16,
  input  in_17,
  output co,
  output out_19,
  output out_20,
  output out_21,
  output out_22,
  output out_23,
  output out_24,
  output out_25,
  output out_26
);

  wire fulladder_2_co, fulladder_3_co, fulladder_4_co, fulladder_5_co, fulladder_6_co, fulladder_7_co,
       fulladder_8_co;

  fulladder fulladder_1 (.a(in_2), .b(in_1), .s(out_19), .co(co), .ci(fulladder_2_co));
  fulladder fulladder_2 (.a(in_4), .b(in_3), .s(out_20), .co(fulladder_2_co), .ci(fulladder_3_co));
  fulladder fulladder_3 (.a(in_6), .b(in_5), .s(out_21), .co(fulladder_3_co), .ci(fulladder_4_co));
  fulladder fulladder_4 (.a(in_8), .b(in_7), .s(out_22), .co(fulladder_4_co), .ci(fulladder_5_co));
  fulladder fulladder_5 (.a(in_10), .b(in_9), .s(out_23), .co(fulladder_5_co), .ci(fulladder_6_co));
  fulladder fulladder_6 (.a(in_12), .b(in_11), .s(out_24), .co(fulladder_6_co), .ci(fulladder_7_co));
  fulladder fulladder_7 (.a(in_14), .b(in_13), .s(out_25), .co(fulladder_7_co), .ci(fulladder_8_co));
  fulladder fulladder_8 (.a(in_16), .b(in_15), .s(out_26), .co(fulladder_8_co), .ci(in_17));
endmodule

module clock (
  output out_1
);

  wire clock_1_out, not_1_out, not_2_out;

  Clock clock_1 (.out(clock_1_out));
  not not_1 (not_1_out, clock_1_out);
  not not_2 (not_2_out, not_1_out);
  and and_1 (out_1, clock_1_out, not_2_out);
endmodule

module srlatch (
  output o,
  output \do 
);

  wire reset_out, set_out;

  Button set (.out(set_out));
  Button reset (.out(reset_out));
  nor nor_1 (o, set_out, \do );
  nor nor_2 (\do , o, reset_out);
endmodule

module dlatch (
  input  en,
  input  D,
  output out
);

  wire and_1_out, and_2_out, nor_2_out, not_1_out;

  not not_1 (not_1_out, D);
  and and_1 (and_1_out, not_1_out, en);
  and and_2 (and_2_out, en, D);
  nor nor_1 (out, and_1_out, nor_2_out);
  nor nor_2 (nor_2_out, out, and_2_out);

  // Notes on the sheet:
  //   https://medium.com/@karlrombauts/building-an-8-bit-computer-in-logisim-part-1-building-blocks-a4f1e5ea0d03
endmodule
