// Logisim project gates.circ as structural Verilog
module main (
  input  in_1,
  input  in_2,
  input  in_3,
  output out_4
);

  wire n7404_1_p2, n7404_1_p3, n7408_1_p3;

  // _7404 7404_1: pin names not known; wires that end beside it: in_2, n7404_1_p2, n7404_1_p3
  // _7408 7408_1: pin names not known; wires that end beside it: in_1, n7404_1_p2, n7408_1_p3, in_2, in_3
  // _7432 7432_1: pin names not known; wires that end beside it: n7408_1_p3, n7404_1_p3, out_4
endmodule
